// Logisim project SOP_Simplification_1st_Display.circ as structural Verilog: 1 circuit, main circuit main
module main (
  input  X,
  input  Y,
  input  Z
);

  wire a_out, and_1_out, and_2_out, and_3_out, and_4_out, and_5_out, and_6_out, and_7_out, and_8_out, c_out,
       d_out, e_out, f_out, g_out, not_1_out, not_2_out, not_3_out, or_1_out;

  not not_1 (not_1_out, X);
  not not_2 (not_2_out, Z);
  not not_3 (not_3_out, Y);
  or a (a_out, X, Y, Z);
  and and_1 (and_1_out, not_1_out, not_3_out);
  and and_2 (and_2_out, Y, not_2_out);
  and and_3 (and_3_out, Y, not_2_out);
  and and_4 (and_4_out, X, not_3_out);
  and and_5 (and_5_out, not_1_out, not_2_out);
  and and_6 (and_6_out, not_1_out, Y);
  and and_7 (and_7_out, X, Z);
  or or_1 (or_1_out, and_1_out, not_2_out);
  and and_8 (and_8_out, Y, Z);
  or c (c_out, and_1_out, and_2_out);
  or d (d_out, and_3_out, X);
  or f (f_out, and_5_out, and_6_out, and_7_out);
  or e (e_out, and_4_out, and_8_out);
  or g (g_out, Y, not_2_out);
  _7_Segment_Display u_7_segment_display_1 (
    .g(g_out), .f(f_out), .a(a_out), .b(or_1_out), .e(e_out), .d(d_out), .c(c_out));  // open: dp
endmodule
